# Fritzing sketch digital temperature sensor module (saved by Fritzing 0.9.3b)

parts:
  Part1 = KY-028 Digital Temperature Sensor Module [package="Breakout board"]
  Componente1 = Arduino Uno (Rev3) - ICSP

nets:
  N1: Part1.A0, Componente1.A0
  N2: Part1.G, Componente1.GND
  N3: Part1.+, Componente1.5V

custom parts:
  KY-028 Digital Temperature Sensor Module: KEYES KY-028 Digital Temperature Sensor Module, used to measure changes in temperature.
